# Fritzing sketch silentglade (saved by Fritzing 0.9.3b)
perfboards: 1

parts:
  R1 = Rotary Potentiometer (Small) [maximum_resistance=1kΩ package=THT]
  R2 = Photocell (LDR) [package=THT]
  Q1 = MOSFET-NCHANNEL [package=to-92]

nets:
  to button: R1.wiper, R2.pin_1, Q1.D
  5V: R1.leg2
  GND: R2.pin_0, Q1.S
